# Fritzing sketch Traffic Light fritzing diagram (saved by Fritzing 0.9.3b)
breadboards: 1

parts:
  Part1 = Arduino Uno (Rev3)
  R1 = Resistor [tolerance=±5% resistance=220 package="2512 [SMD]"]
  R2 = Resistor [tolerance=±5% resistance=220 package="2512 [SMD]"]
  R3 = Resistor [tolerance=±5% resistance=220 package="2512 [SMD]"]
  R4 = Resistor [tolerance=±5% resistance=220 package="2512 [SMD]"]
  R5 = Resistor [tolerance=±5% resistance=220 package="2512 [SMD]"]
  R6 = Resistor [tolerance=±5% resistance=220 package="2512 [SMD]"]
  DI1 = 7-Segment LED Display [package=THT]
  R7 = Resistor [tolerance=±5% resistance=220 package="2512 [SMD]"]
  R8 = Resistor [tolerance=±5% resistance=220 package="2512 [SMD]"]
  U1 = 74HC595 SMD [package="SO16 [SMD]"]
  R9 = Resistor [tolerance=±5% resistance=220 package="2512 [SMD]"]
  R10 = Resistor [tolerance=±5% resistance=220 package="2512 [SMD]"]
  R11 = Resistor [tolerance=±5% resistance=220 package="2512 [SMD]"]
  LED1 = smd LED [color="Red (633nm)" package="1206 [SMD]"]
  LED2 = smd LED [color="Yellow (595nm)" package="1206 [SMD]"]
  LED3 = smd LED [color="Green (565nm)" package="1206 [SMD]"]
  LED4 = smd LED [color="Red (633nm)" package="1206 [SMD]"]
  LED5 = smd LED [color="Green (565nm)" package="1206 [SMD]"]
  LED6 = smd LED [color="Yellow (595nm)" package="1206 [SMD]"]
  R13 = Resistor [tolerance=±5% resistance=220 package="2512 [SMD]"]
  R14 = Resistor [tolerance=±5% resistance=220 package="2512 [SMD]"]
  R15 = Resistor [tolerance=±5% resistance=220 package="2512 [SMD]"]
  C1 = Electrolytic Capacitor [capacitance=10µF voltage=10V package="100 mil [THT, electrolytic]"]
  S1 = Momentary Switch [package=ksa_sealed_tac_switch]
  S2 = Momentary Switch [package=ksa_sealed_tac_switch]
  R17 = Resistor [tolerance=±5% resistance=10k package=THT]
  R18 = Resistor [tolerance=±5% resistance=10k package=THT]
  R19 = Resistor [tolerance=±5% resistance=10k package=THT]
  S3 = Momentary Switch [package=ksa_sealed_tac_switch]
  R20 = Photocell (LDR) [package=THT]
  R21 = Resistor [tolerance=±5% resistance=10k package=THT]
  R22 = Resistor [tolerance=±5% resistance=220 package="2010 [SMD]"]
  J1 = Piezo Speaker
  J2 = Basic Servo

nets:
  N1: Part1.A0, R20.pin_0, R21.Pin_1
  N2: Part1.A3, S2.3, R18.Pin_1
  N3: Part1.A4/SDA, R17.Pin_1, S3.4
  N4: Part1.A5/SCL, S1.1, R19.Pin_0
  N5: Part1.D8, R11.Pin_0
  N6: Part1.D9_PWM, R10.Pin_0
  N7: Part1.D10_PWM/SS, R9.Pin_0
  N8: Part1.D11_PWM/MOSI, R15.Pin_0
  N9: Part1.D12/MISO, R14.Pin_0
  N10: Part1.D13/SCK, R13.Pin_0
  N11: Part1.D3_PWM, R22.Pin_1
  N12: Part1.D4, J2.pulse
  N13: Part1.D5_PWM, U1.DS
  N14: Part1.D6_PWM, U1.ST_CP
  N15: Part1.D7, U1.SH_CP
  N16: R1.Pin_0, DI1.cathodeB
  VCC: R1.Pin_1, U1.MR, U1.VCC, C1.+, R17.Pin_0, R18.Pin_0, R19.Pin_1, R20.pin_1, J2.vcc
  N17: R2.Pin_0, DI1.cathodeA
  N18: R2.Pin_1, U1.Q0
  N19: R3.Pin_0, DI1.cathodeC
  N20: R3.Pin_1, U1.Q2
  N21: R4.Pin_0, DI1.cathodeDP
  N22: R4.Pin_1, U1.Q1
  N23: R5.Pin_0, U1.Q3
  N24: R5.Pin_1, DI1.cathodeD
  N25: R6.Pin_0, U1.Q4
  N26: R6.Pin_1, DI1.cathodeE
  GND: DI1.commAnode#7, U1.GND, U1.OE, LED1.cathode, LED2.cathode, LED3.cathode, LED4.cathode, LED5.cathode, LED6.cathode, C1.-, S1.3, S2.1, S3.2, R21.Pin_0, J1.pin1, J2.gnd
  N27: DI1.cathodeF, R7.Pin_1
  N28: DI1.cathodeG, R8.Pin_1
  N29: R7.Pin_0, U1.Q5
  N30: R8.Pin_0, U1.Q6
  N31: R9.Pin_1, LED1.anode
  N32: R10.Pin_1, LED2.anode
  N33: R11.Pin_1, LED3.anode
  N34: LED4.anode, R13.Pin_1
  N35: LED5.anode, R15.Pin_1
  N36: LED6.anode, R14.Pin_1
  N37: R22.Pin_0, J1.pin2
