# Fritzing sketch Traffic Light fritzing diagram (saved by Fritzing 0.9.3b)
breadboards: 1

parts:
  Part1 = Arduino Uno (Rev3)
  R1 = Resistor [tolerance=±5% resistance=220 package="2512 [SMD]"]
  R2 = Resistor [tolerance=±5% resistance=220 package="2512 [SMD]"]
  R3 = Resistor [tolerance=±5% resistance=220 package="2512 [SMD]"]
  R4 = Resistor [tolerance=±5% resistance=220 package="2512 [SMD]"]
  R5 = Resistor [tolerance=±5% resistance=220 package="2512 [SMD]"]
  R6 = Resistor [tolerance=±5% resistance=220 package="2512 [SMD]"]
  DI1 = 7-Segment LED Display [package=THT]
  R7 = Resistor [tolerance=±5% resistance=220 package="2512 [SMD]"]
  R8 = Resistor [tolerance=±5% resistance=220 package="2512 [SMD]"]
  U1 = 74HC595 SMD [package="SO16 [SMD]"]
  R9 = Resistor [tolerance=±5% resistance=220 package="2512 [SMD]"]
  R10 = Resistor [tolerance=±5% resistance=220 package="2512 [SMD]"]
  R11 = Resistor [tolerance=±5% resistance=220 package="2512 [SMD]"]
  LED1 = smd LED [color="Red (633nm)" package="1206 [SMD]"]
  LED2 = smd LED [color="Yellow (595nm)" package="1206 [SMD]"]
  LED3 = smd LED [color="Green (565nm)" package="1206 [SMD]"]
  LED4 = smd LED [color="Red (633nm)" package="1206 [SMD]"]
  LED5 = smd LED [color="Green (565nm)" package="1206 [SMD]"]
  LED6 = smd LED [color="Yellow (595nm)" package="1206 [SMD]"]
  R13 = Resistor [tolerance=±5% resistance=220 package="2512 [SMD]"]
  R14 = Resistor [tolerance=±5% resistance=220 package="2512 [SMD]"]
  R15 = Resistor [tolerance=±5% resistance=220 package="2512 [SMD]"]
  R16 = Resistor [tolerance=±5% resistance=220 package="2512 [SMD]"]
  J1 = Piezo Speaker
  C1 = Electrolytic Capacitor [capacitance=10µF voltage=10V package="100 mil [THT, electrolytic]"]
  J2 = Basic Servo

nets:
  N1: Part1.D3_PWM, R16.Pin_1
  N2: Part1.D4, J2.pulse
  N3: Part1.D5_PWM, U1.DS
  N4: Part1.D6_PWM, U1.ST_CP
  N5: Part1.D7, U1.SH_CP
  N6: R1.Pin_0, DI1.cathodeB
  N7: R1.Pin_1, U1.Q0
  N8: R2.Pin_0, DI1.cathodeA
  N9: R3.Pin_0, DI1.cathodeC
  N10: R4.Pin_0, DI1.cathodeDP
  N11: R5.Pin_1, DI1.cathodeD
  N12: R6.Pin_1, DI1.cathodeE
  N13: DI1.commAnode#7, U1.OE, LED1.cathode, LED2.cathode, LED3.cathode, LED4.cathode, LED5.cathode, LED6.cathode, J1.pin1, C1.-, J2.gnd
  N14: DI1.cathodeF, R7.Pin_1
  N15: DI1.cathodeG, R8.Pin_1
  VCC: U1.MR, U1.VCC, C1.+, J2.vcc
  N16: R9.Pin_1, LED1.anode
  N17: R10.Pin_1, LED2.anode
  N18: R11.Pin_1, LED3.anode
  N19: LED4.anode, R13.Pin_1
  N20: LED5.anode, R15.Pin_1
  N21: LED6.anode, R14.Pin_1
  N22: R16.Pin_0, J1.pin2
